// Logisim project project.circ as structural Verilog: 10 circuits, main circuit main
module main (
  output [3:0] out_1
);

  wire CPU_CLOCK_out;
  wire [3:0] INC_sum;

  Clock CPU_CLOCK (.out(CPU_CLOCK_out));
  _4bit_Register PC (.in_1(CPU_CLOCK_out), .in_2(INC_sum), .out_3(out_1));
  _4_bit_adder INC (.in_1(4'b0001), .in_2(out_1), .Sum(INC_sum));  // open: Overflow
endmodule

module _8bit_Register (
  input  clock_input,
  input  [7:0] in_2,
  output [7:0] out_3
);

  D_Flip_Flop d_ff_1 (.clk(clock_input), .D(in_2[6]), .Q(out_3[6]));  // open: Qn, preset, en, reset
  D_Flip_Flop d_ff_2 (.clk(clock_input), .D(in_2[7]), .Q(out_3[7]));  // open: Qn, preset, en, reset
  D_Flip_Flop d_ff_3 (.clk(clock_input), .D(in_2[5]), .Q(out_3[5]));  // open: Qn, preset, en, reset
  D_Flip_Flop d_ff_4 (.clk(clock_input), .D(in_2[4]), .Q(out_3[4]));  // open: Qn, preset, en, reset
  D_Flip_Flop d_ff_5 (.clk(clock_input), .D(in_2[3]), .Q(out_3[3]));  // open: Qn, preset, en, reset
  D_Flip_Flop d_ff_6 (.clk(clock_input), .D(in_2[2]), .Q(out_3[2]));  // open: Qn, preset, en, reset
  D_Flip_Flop d_ff_7 (.clk(clock_input), .D(in_2[1]), .Q(out_3[1]));  // open: Qn, preset, en, reset
  D_Flip_Flop d_ff_8 (.clk(clock_input), .D(in_2[0]), .Q(out_3[0]));  // open: Qn, preset, en, reset
endmodule

module _4bit_Register (
  input  in_1,
  input  [3:0] in_2,
  output [3:0] out_3
);

  wire d_ff_1_qn, d_ff_5_qn, undriven, undriven_2, undriven_3, undriven_4, undriven_5, undriven_6;

  D_Flip_Flop d_ff_1 (
    .clk(in_1), .D(in_2[3]), .Q(out_3[3]), .Qn(d_ff_1_qn), .preset(undriven), .en(undriven_2),
    .reset(undriven_3));
  D_Flip_Flop d_ff_2 (.clk(in_1), .D(in_2[2]), .Q(out_3[2]));  // open: Qn, preset, en, reset
  D_Flip_Flop d_ff_3 (
    .clk(in_1), .D(in_2[3]), .Q(out_3[3]), .Qn(d_ff_1_qn), .preset(undriven), .en(undriven_2),
    .reset(undriven_3));
  D_Flip_Flop d_ff_4 (.clk(in_1), .D(in_2[1]), .Q(out_3[1]));  // open: Qn, preset, en, reset
  D_Flip_Flop d_ff_5 (
    .clk(in_1), .D(in_2[0]), .Q(out_3[0]), .Qn(d_ff_5_qn), .preset(undriven_4), .en(undriven_5),
    .reset(undriven_6));
  D_Flip_Flop d_ff_6 (
    .clk(in_1), .D(in_2[0]), .Q(out_3[0]), .Qn(d_ff_5_qn), .preset(undriven_4), .en(undriven_5),
    .reset(undriven_6));
endmodule

module half_adder (
  input  in_1,
  input  in_2,
  output sum_out,
  output carry_out
);

  xor xor_1 (sum_out, in_1, in_2);
  and and_1 (carry_out, in_1, in_2);
endmodule

module full_adder (
  input  in_1,
  input  in_2,
  input  carry,
  output carry_out,
  output sum_out
);

  wire half_adder_2_carry_out, half_adder_carry_out, half_adder_sum_out;

  half_adder half_adder (.in_1(in_1), .in_2(in_2), .sum_out(half_adder_sum_out), .carry_out(half_adder_carry_out));
  half_adder half_adder_2 (
    .in_1(half_adder_sum_out), .in_2(carry), .sum_out(sum_out), .carry_out(half_adder_2_carry_out));
  or or_1 (carry_out, half_adder_carry_out, half_adder_2_carry_out);
endmodule

module _4_bit_adder (
  input  [3:0] in_1,
  input  [3:0] in_2,
  output Overflow,
  output [3:0] Sum
);

  wire full_adder_1_carry_out, full_adder_3_carry_out, half_adder_1_carry_out;

  half_adder half_adder_1 (.in_1(in_1[0]), .in_2(in_2[0]), .sum_out(Sum[0]), .carry_out(half_adder_1_carry_out));
  full_adder full_adder_1 (
    .in_1(in_1[1]), .in_2(in_2[1]), .carry(half_adder_1_carry_out), .carry_out(full_adder_1_carry_out),
    .sum_out(Sum[1]));
  full_adder full_adder_2 (
    .in_1(in_1[3]), .in_2(in_2[3]), .carry(full_adder_3_carry_out), .carry_out(Overflow), .sum_out(Sum[3]));
  full_adder full_adder_3 (
    .in_1(in_1[2]), .in_2(in_2[2]), .carry(full_adder_1_carry_out), .carry_out(full_adder_3_carry_out),
    .sum_out(Sum[2]));
endmodule

module display (
  input  [7:0] in_1
);

  wire addif5_1_out_6, addif5_1_out_7, addif5_1_out_8, addif5_1_out_9, addif5_2_out_6, addif5_2_out_7,
       addif5_2_out_8, addif5_2_out_9, addif5_3_out_6, addif5_3_out_7, addif5_3_out_8, addif5_3_out_9,
       addif5_4_out_6, addif5_4_out_7, addif5_4_out_8, addif5_4_out_9, addif5_5_out_6, addif5_5_out_7,
       addif5_5_out_8, addif5_5_out_9, addif5_6_out_6, addif5_6_out_7, addif5_6_out_8, addif5_6_out_9,
       addif5_7_out_6, addif5_7_out_7, addif5_7_out_8, addif5_7_out_9, n2bitdisplay_1_s1, n2bitdisplay_1_s2,
       n2bitdisplay_1_s3, n2bitdisplay_1_s4, n2bitdisplay_1_s5, n2bitdisplay_1_s6, n2bitdisplay_1_s7,
       n2bitdisplay_1_s8, n4bitdisplay_1_out_5, n4bitdisplay_1_out_6, n4bitdisplay_1_out_7,
       n4bitdisplay_1_out_8, n4bitdisplay_1_out_9, n4bitdisplay_1_out_10, n4bitdisplay_1_out_11,
       n4bitdisplay_1_out_12, n4bitdisplay_2_out_5, n4bitdisplay_2_out_6, n4bitdisplay_2_out_7,
       n4bitdisplay_2_out_8, n4bitdisplay_2_out_9, n4bitdisplay_2_out_10, n4bitdisplay_2_out_11,
       n4bitdisplay_2_out_12;

  _2bitdisplay u_2bitdisplay_1 (
    .a(addif5_1_out_9), .b(addif5_2_out_9), .s1(n2bitdisplay_1_s1), .s2(n2bitdisplay_1_s2),
    .s3(n2bitdisplay_1_s3), .s4(n2bitdisplay_1_s4), .s5(n2bitdisplay_1_s5), .s6(n2bitdisplay_1_s6),
    .s7(n2bitdisplay_1_s7), .s8(n2bitdisplay_1_s8));
  _7_Segment_Display u_7_segment_display_1 (
    .g(n2bitdisplay_1_s1), .f(n2bitdisplay_1_s2), .a(n2bitdisplay_1_s3), .b(n2bitdisplay_1_s4),
    .e(n2bitdisplay_1_s5), .d(n2bitdisplay_1_s6), .c(n2bitdisplay_1_s7), .dp(n2bitdisplay_1_s8));
  addif5 addif5_1 (
    .in_1(addif5_5_out_9), .in_2(addif5_4_out_9), .in_3(addif5_3_out_9), .in_4(1'b0), .out_6(addif5_1_out_6),
    .out_7(addif5_1_out_7), .out_8(addif5_1_out_8), .out_9(addif5_1_out_9));  // open: Overflow
  addif5 addif5_2 (
    .in_1(addif5_6_out_9), .in_2(addif5_1_out_6), .in_3(addif5_1_out_7), .in_4(addif5_1_out_8),
    .out_6(addif5_2_out_6), .out_7(addif5_2_out_7), .out_8(addif5_2_out_8), .out_9(addif5_2_out_9));  // open: Overflow
  addif5 addif5_3 (
    .in_1(in_1[5]), .in_2(in_1[6]), .in_3(in_1[7]), .in_4(1'b0), .out_6(addif5_3_out_6),
    .out_7(addif5_3_out_7), .out_8(addif5_3_out_8), .out_9(addif5_3_out_9));  // open: Overflow
  addif5 addif5_4 (
    .in_1(in_1[4]), .in_2(addif5_3_out_6), .in_3(addif5_3_out_7), .in_4(addif5_3_out_8),
    .out_6(addif5_4_out_6), .out_7(addif5_4_out_7), .out_8(addif5_4_out_8), .out_9(addif5_4_out_9));  // open: Overflow
  addif5 addif5_5 (
    .in_1(in_1[3]), .in_2(addif5_4_out_6), .in_3(addif5_4_out_7), .in_4(addif5_4_out_8),
    .out_6(addif5_5_out_6), .out_7(addif5_5_out_7), .out_8(addif5_5_out_8), .out_9(addif5_5_out_9));  // open: Overflow
  addif5 addif5_6 (
    .in_1(in_1[2]), .in_2(addif5_5_out_6), .in_3(addif5_5_out_7), .in_4(addif5_5_out_8),
    .out_6(addif5_6_out_6), .out_7(addif5_6_out_7), .out_8(addif5_6_out_8), .out_9(addif5_6_out_9));  // open: Overflow
  addif5 addif5_7 (
    .in_1(in_1[1]), .in_2(addif5_6_out_6), .in_3(addif5_6_out_7), .in_4(addif5_6_out_8),
    .out_6(addif5_7_out_6), .out_7(addif5_7_out_7), .out_8(addif5_7_out_8), .out_9(addif5_7_out_9));  // open: Overflow
  _7_Segment_Display u_7_segment_display_2 (
    .g(n4bitdisplay_1_out_5), .f(n4bitdisplay_1_out_6), .a(n4bitdisplay_1_out_7), .b(n4bitdisplay_1_out_8),
    .e(n4bitdisplay_1_out_9), .d(n4bitdisplay_1_out_10), .c(n4bitdisplay_1_out_11), .dp(n4bitdisplay_1_out_12));
  _4bitdisplay u_4bitdisplay_1 (
    .a(addif5_2_out_8), .b(addif5_2_out_7), .c(addif5_2_out_6), .d(addif5_7_out_9),
    .out_9(n4bitdisplay_1_out_9), .out_10(n4bitdisplay_1_out_10), .out_11(n4bitdisplay_1_out_11),
    .out_12(n4bitdisplay_1_out_12), .out_5(n4bitdisplay_1_out_5), .out_6(n4bitdisplay_1_out_6),
    .out_7(n4bitdisplay_1_out_7), .out_8(n4bitdisplay_1_out_8));
  _4bitdisplay u_4bitdisplay_2 (
    .a(addif5_7_out_8), .b(addif5_7_out_7), .c(addif5_7_out_6), .d(in_1[0]), .out_9(n4bitdisplay_2_out_9),
    .out_10(n4bitdisplay_2_out_10), .out_11(n4bitdisplay_2_out_11), .out_12(n4bitdisplay_2_out_12),
    .out_5(n4bitdisplay_2_out_5), .out_6(n4bitdisplay_2_out_6), .out_7(n4bitdisplay_2_out_7),
    .out_8(n4bitdisplay_2_out_8));
  _7_Segment_Display u_7_segment_display_3 (
    .g(n4bitdisplay_2_out_5), .f(n4bitdisplay_2_out_6), .a(n4bitdisplay_2_out_7), .b(n4bitdisplay_2_out_8),
    .e(n4bitdisplay_2_out_9), .d(n4bitdisplay_2_out_10), .c(n4bitdisplay_2_out_11), .dp(n4bitdisplay_2_out_12));

  // Notes on the sheet:
  //   hunds
  //   tens
  //   ones
endmodule

module addif5 (
  input  in_1,
  input  in_2,
  input  in_3,
  input  in_4,
  output Overflow,
  output out_6,
  output out_7,
  output out_8,
  output out_9
);

  wire and_1_out, full_adder_1_carry_out, full_adder_2_carry_out, half_adder_1_carry_out, or_1_out, or_2_out;
  wire [3:0] half_adder_1_sum_out;

  or or_1 (or_1_out, in_2, in_1);
  and and_1 (and_1_out, in_3, or_1_out);
  or or_2 (or_2_out, in_4, and_1_out);
  full_adder full_adder_1 (
    .in_1(1'b1), .in_2(in_2), .carry(half_adder_1_carry_out), .carry_out(full_adder_1_carry_out),
    .sum_out(half_adder_1_sum_out[1]));
  half_adder half_adder_1 (
    .in_1(1'b1), .in_2(in_1), .sum_out(half_adder_1_sum_out[0]), .carry_out(half_adder_1_carry_out));
  Multiplexer #(.width(4), .enable("false")) multiplexer_1 (
    .in0({in_4, in_3, in_2, in_1}), .in1(half_adder_1_sum_out), .out({out_9, out_8, out_7, out_6}),
    .sel(or_2_out));
  full_adder full_adder_2 (
    .in_1(1'b0), .in_2(in_3), .carry(full_adder_1_carry_out), .carry_out(full_adder_2_carry_out),
    .sum_out(half_adder_1_sum_out[2]));
  full_adder full_adder_3 (
    .in_1(1'b0), .in_2(in_4), .carry(full_adder_2_carry_out), .carry_out(Overflow),
    .sum_out(half_adder_1_sum_out[3]));
endmodule

module _4bitdisplay (
  input  a,
  input  b,
  input  c,
  input  d,
  output out_5,
  output out_6,
  output out_7,
  output out_8,
  output out_9,
  output out_10,
  output out_11,
  output out_12
);

  wire and_1_out, and_2_out, and_3_out, and_4_out, and_5_out, and_6_out, and_7_out, and_8_out, and_9_out,
       and_10_out, and_11_out, and_12_out, and_13_out, and_14_out, and_15_out, and_16_out, and_17_out,
       and_18_out, and_19_out, and_20_out, and_21_out, and_22_out, and_23_out, and_24_out, and_25_out,
       and_26_out, not_1_out, not_2_out, not_3_out, not_4_out, not_5_out, not_6_out, not_7_out, not_8_out,
       not_9_out, not_10_out, not_11_out, not_12_out, not_13_out, not_14_out, not_15_out, not_16_out,
       not_17_out, not_18_out, not_19_out, not_20_out, not_21_out, not_22_out, not_23_out, not_24_out,
       not_25_out, not_26_out, not_27_out, not_28_out, not_29_out, not_30_out, not_31_out, not_32_out,
       not_33_out, not_34_out, not_35_out, not_36_out, not_37_out, not_38_out, not_39_out, not_40_out,
       not_41_out, not_42_out, not_43_out, not_44_out, not_45_out, not_46_out, not_47_out, not_48_out,
       not_49_out, not_50_out, not_51_out, not_52_out, not_53_out;

  not not_1 (not_1_out, a);
  and and_1 (and_1_out, not_1_out, not_2_out, c);
  not not_2 (not_2_out, b);
  not not_3 (not_3_out, a);
  and and_2 (and_2_out, not_3_out, b, not_4_out);
  not not_4 (not_4_out, c);
  not not_5 (not_5_out, a);
  and and_3 (and_3_out, not_5_out, b, not_6_out);
  not not_6 (not_6_out, d);
  and and_4 (and_4_out, a, not_7_out, not_8_out);
  not not_7 (not_7_out, b);
  not not_8 (not_8_out, c);
  not not_9 (not_9_out, a);
  not not_10 (not_10_out, c);
  and and_5 (and_5_out, not_9_out, not_10_out, not_11_out);
  not not_11 (not_11_out, d);
  not not_12 (not_12_out, a);
  and and_6 (and_6_out, not_12_out, b, not_13_out);
  not not_13 (not_13_out, c);
  not not_14 (not_14_out, a);
  and and_7 (and_7_out, not_14_out, b, not_15_out);
  not not_15 (not_15_out, d);
  and and_8 (and_8_out, a, not_16_out, not_17_out);
  not not_16 (not_16_out, b);
  not not_17 (not_17_out, c);
  not not_18 (not_18_out, a);
  and and_9 (and_9_out, not_18_out, not_19_out, not_20_out);
  not not_19 (not_19_out, b);
  not not_20 (not_20_out, d);
  not not_21 (not_21_out, a);
  and and_10 (and_10_out, not_21_out, c);
  not not_22 (not_22_out, a);
  and and_11 (and_11_out, not_22_out, b, d);
  not not_23 (not_23_out, b);
  and and_12 (and_12_out, a, not_23_out, not_24_out);
  not not_24 (not_24_out, c);
  not not_25 (not_25_out, a);
  and and_13 (and_13_out, not_25_out, not_26_out);
  not not_26 (not_26_out, b);
  not not_27 (not_27_out, a);
  and and_14 (and_14_out, not_27_out, not_28_out, not_29_out);
  not not_28 (not_28_out, c);
  not not_29 (not_29_out, d);
  not not_30 (not_30_out, b);
  and and_15 (and_15_out, not_30_out, not_31_out);
  not not_31 (not_31_out, c);
  not not_32 (not_32_out, a);
  and and_16 (and_16_out, not_32_out, c, d);
  not not_33 (not_33_out, a);
  not not_34 (not_34_out, b);
  and and_17 (and_17_out, not_33_out, not_34_out, not_35_out);
  not not_35 (not_35_out, d);
  not not_36 (not_36_out, b);
  not not_37 (not_37_out, c);
  and and_18 (and_18_out, not_36_out, not_37_out, not_38_out);
  not not_38 (not_38_out, d);
  not not_39 (not_39_out, a);
  and and_19 (and_19_out, not_39_out, c, not_40_out);
  not not_40 (not_40_out, d);
  not not_41 (not_41_out, b);
  not not_42 (not_42_out, c);
  not not_43 (not_43_out, d);
  not not_44 (not_44_out, a);
  not not_45 (not_45_out, b);
  not not_46 (not_46_out, a);
  not not_47 (not_47_out, d);
  not not_48 (not_48_out, a);
  not not_49 (not_49_out, c);
  not not_50 (not_50_out, b);
  and and_20 (and_20_out, not_50_out, not_51_out);
  not not_51 (not_51_out, c);
  not not_52 (not_52_out, a);
  and and_21 (and_21_out, not_52_out, d);
  not not_53 (not_53_out, a);
  and and_22 (and_22_out, not_53_out, b);
  or or_1 (out_5, and_1_out, and_2_out, and_3_out, and_4_out);
  or or_2 (out_6, and_5_out, and_6_out, and_7_out, and_8_out);
  or or_3 (out_7, and_9_out, and_10_out, and_11_out, and_12_out);
  or or_4 (out_8, and_13_out, and_14_out, and_15_out, and_16_out);
  or or_5 (out_9, and_17_out, and_18_out, and_19_out);
  and and_23 (and_23_out, not_41_out, not_42_out, not_43_out);
  and and_24 (and_24_out, not_44_out, not_45_out, c);
  and and_25 (and_25_out, not_46_out, c, not_47_out);
  and and_26 (and_26_out, not_48_out, b, not_49_out, d);
  or or_6 (out_11, and_20_out, and_21_out, and_22_out);
  or or_7 (out_10, and_23_out, and_24_out, and_25_out, and_26_out);

  assign out_12 = 1'b0;
endmodule

module _2bitdisplay (
  input  a,
  input  b,
  output s1,
  output s2,
  output s3,
  output s4,
  output s5,
  output s6,
  output s7,
  output s8
);

  wire not_1_out, not_2_out, not_3_out, not_5_out, not_6_out;

  not not_1 (not_1_out, b);
  not not_2 (not_2_out, a);
  not not_3 (not_3_out, b);
  not not_4 (s3, b);
  not not_5 (not_5_out, a);
  not not_6 (not_6_out, b);
  not not_7 (s5, b);
  not not_8 (s6, b);
  not not_9 (s7, a);
  and and_1 (s1, a, not_1_out);
  and and_2 (s2, not_2_out, not_3_out);
  or or_1 (s4, not_5_out, not_6_out);

  assign s8 = 1'b0;
endmodule
